// Logisim project main.circ as structural Verilog: 2 circuits, main circuit main
module main (
);

  wire [23:0] Program_data;

  ROM #(.addrWidth(16), .dataWidth(24), .Select("low")) Program (.data(Program_data));  // open: addr
  alu ALU ();  // open: A, B, ALU_OP, IN_FLAGS, OUT, OUT_FLAGS

  // Notes on the sheet:
  //   Main architecture
  //   OPCODE here
endmodule

module alu (
  input  [15:0] A,
  input  [15:0] B,
  input  [3:0] ALU_OP,
  input  [3:0] IN_FLAGS,
  output [15:0] OUT,
  output [3:0] OUT_FLAGS
);

  wire [15:0] adder_1_out;

  Adder #(.width(16)) adder_1 (.a(A), .b(B), .out(adder_1_out), .cin(IN_FLAGS[0]));  // open: cout
  Multiplexer #(.select(4), .width(16), .enable("false")) multiplexer_1 (
    .in0(adder_1_out), .sel(ALU_OP));  // open: in1, in2, in3, in4, in5, in6, in7, in8, in9, in10, in11, in12, in13, in14, in15, out

  // Notes on the sheet:
  //   ALU interface
endmodule
